# Fritzing sketch circuit (saved by Fritzing 0.9.9b)
breadboards: 1

parts:
  J1 = STM32 Nucleo boards
  Driver1 = 28BYJ-48 Driver Module [part_number=ULN2003 package=THT]
  SM1 = 28BYJ-48 Stepper Motor [part_number=28BYJ-48]
  Load_Cell1 = Load Cell - Red/white/black/green
  Componente1 = HX711 Weighing Sensor Module
  OLED_I2C1 = OLED 128x64 I2C Monochrome Display
  HC-SR04_Sensor_1 = HC-SR04 Ultrasonic Distance Sensor
  R1 = Resistor [tolerance=±5% resistance=220 package="0805 [SMD]"]
  S1 = Pushbutton [package="[THT]"]

nets:
  N1: J1.D8, HC-SR04_Sensor_1.TRIG
  N2: J1.D9_PWM, HC-SR04_Sensor_1.ECHO
  N3: J1.D11_PWM/MOSI, Componente1.DO/RX
  N4: J1.D12/MISO, Componente1.CK/TX
  N5: J1.D13/SCK, R1.Pin_0, S1.Pin_1, S1.Pin_2
  N6: J1.A4/SDA, OLED_I2C1.GND
  N7: J1.A5/SCL, OLED_I2C1.VDD
  N8: J1.D3_PWM, Driver1.IN3
  N9: J1.D4, Driver1.IN1
  N10: J1.D5_PWM, Driver1.IN2
  N11: J1.D7, Driver1.IN4
  N12: J1.3V3, OLED_I2C1.SCK
  VCC: J1.5V, Driver1.Vmotor, Componente1.VCC, HC-SR04_Sensor_1.VCC, S1.Pin_3, S1.Pin_4
  GND: J1.GND, Driver1.GND, Componente1.GND, OLED_I2C1.SDA, HC-SR04_Sensor_1.GND, R1.Pin_1
  N13: Driver1.blue-pin, SM1.blue-pin
  N14: Driver1.pink-pin, SM1.pink-pin
  N15: Driver1.yellow-pin, SM1.yellow-pin
  N16: Driver1.orange-pin, SM1.orange-pin
  N17: Driver1.red-pin, SM1.red-pin
  N18: Load_Cell1.wire1, Componente1.A+
  N19: Load_Cell1.wire2, Componente1.A-
  N20: Load_Cell1.wire3, Componente1.B+
  N21: Load_Cell1.wire4, Componente1.B-

custom parts:
  28BYJ-48 Driver Module: ULN2003 Driver Module for the 28BYJ-48 Unipolar Stepper Motor LED A - Blue wire - Bottom coil left LED B - Pink wire - Top coil left LED C - Yellow wire - Bottom coil right LED D - Orange wire - Top coil right Common rail - red Connector pins: blue - pink - yellow - orange - red Control pins - IN1 to IN4 Power pins - GND & Vmotor (5-12V) On/Off jumper (if removed, power to motor is cut).
  28BYJ-48 Stepper Motor: Unipolar Stepper Motor 28BYJ-48 Top coil - pink & orange Bottom coil - blue & yellow Common rail - red Connector pins: blue - pink - yellow - orange - red
  Load Cell - Red/white/black/green: A rectangle load cell/weighting pressure Sensor with four wires - Red, white, black, green. Normally corresponding with E+, E-, A+, A- respectively.
  HX711 Weighing Sensor Module: HX711 is a precision 24-bit analog-to-digital converter (ADC) designed for weigh scales and industrial control applications to interface directly with a bridge sensor.
